// Logisim project SUMADOR_1BIT.circ as structural Verilog: 1 circuit, main circuit main
module main (
  input  in_1,
  input  in_2,
  input  in_3,
  input  in_4,
  input  in_5,
  output out_6,
  output out_7,
  output Resultado,
  output Acarreo
);

  wire nand_1_out, nand_2_out, nand_3_out, nand_4_out, nand_5_out, nand_6_out, nand_7_out, nand_8_out,
       nand_9_out, nand_10_out, nand_11_out, nand_13_out, nand_14_out, nand_15_out, nand_16_out, nand_17_out,
       nand_18_out;

  nand nand_1 (nand_1_out, in_3, in_4);
  nand nand_2 (nand_2_out, in_3, nand_1_out);
  nand nand_3 (nand_3_out, nand_1_out, in_4);
  nand nand_4 (nand_4_out, in_4, in_3);
  nand nand_5 (nand_5_out, nand_2_out, nand_3_out);
  not nand_6 (nand_6_out, nand_4_out);  // NAND_Gate
  nand nand_7 (nand_7_out, nand_5_out, in_5);
  nand nand_8 (nand_8_out, nand_5_out, nand_7_out);
  nand nand_9 (nand_9_out, nand_7_out, in_5);
  nand nand_10 (nand_10_out, nand_5_out, in_5);
  nand nand_11 (nand_11_out, in_1, in_2);
  nand nand_12 (Resultado, nand_8_out, nand_9_out);
  not nand_13 (nand_13_out, nand_10_out);  // NAND_Gate
  nand nand_14 (nand_14_out, in_1, nand_11_out);
  nand nand_15 (nand_15_out, nand_11_out, in_2);
  nand nand_16 (nand_16_out, in_2, in_1);
  nand nand_17 (nand_17_out, nand_13_out, nand_13_out);
  nand nand_18 (nand_18_out, nand_6_out, nand_6_out);
  nand nand_19 (out_6, nand_14_out, nand_15_out);
  not nand_20 (out_7, nand_16_out);  // NAND_Gate
  nand nand_21 (Acarreo, nand_17_out, nand_18_out);

  // Notes on the sheet:
  //   Sumador SEMICOMPLETO Para 1 BIT
  //    usando solo Compuertas NAND
  //   Circuitos para SUMADOR de 1 BIT usando solo Compuertas NANDS
  //   Sumador COMPLETO Para 1 BIT usando solo Compuertas NAND
endmodule
