// Logisim project SUMADOR_4BITS.circ as structural Verilog: 1 circuit, main circuit main
module main (
  input  in_1,
  input  [3:0] in_2,
  input  [3:0] in_3,
  output Acarreo_final,
  output [4:0] out_5
);

  wire nand_1_out, nand_2_out, nand_3_out, nand_4_out, nand_5_out, nand_6_out, nand_7_out, nand_8_out,
       nand_9_out, nand_10_out, nand_11_out, nand_12_out, nand_13_out, nand_14_out, nand_15_out, nand_16_out,
       nand_17_out, nand_18_out, nand_19_out, nand_20_out, nand_21_out, nand_22_out, nand_23_out,
       nand_24_out, nand_25_out, nand_26_out, nand_27_out, nand_28_out, nand_29_out, nand_30_out,
       nand_31_out, nand_32_out, nand_33_out, nand_34_out, nand_35_out, nand_36_out, nand_37_out,
       nand_38_out, nand_39_out, nand_40_out, nand_42_out, nand_44_out, nand_46_out, nand_48_out,
       nand_49_out, nand_50_out, nand_51_out, nand_52_out, nand_53_out, nand_54_out, nand_55_out,
       nand_56_out, nand_57_out, nand_58_out, nand_59_out;

  nand nand_1 (nand_1_out, in_2[0], in_3[0]);
  nand nand_2 (nand_2_out, in_2[1], in_3[1]);
  nand nand_3 (nand_3_out, in_2[2], in_3[2]);
  nand nand_4 (nand_4_out, in_2[3], in_3[3]);
  nand nand_5 (nand_5_out, in_2[0], nand_1_out);
  nand nand_6 (nand_6_out, nand_1_out, in_3[0]);
  nand nand_7 (nand_7_out, in_3[0], in_2[0]);
  nand nand_8 (nand_8_out, in_2[1], nand_2_out);
  nand nand_9 (nand_9_out, nand_2_out, in_3[1]);
  nand nand_10 (nand_10_out, in_3[1], in_2[1]);
  nand nand_11 (nand_11_out, in_2[2], nand_3_out);
  nand nand_12 (nand_12_out, nand_3_out, in_3[2]);
  nand nand_13 (nand_13_out, in_3[2], in_2[2]);
  nand nand_14 (nand_14_out, in_2[3], nand_4_out);
  nand nand_15 (nand_15_out, nand_4_out, in_3[3]);
  nand nand_16 (nand_16_out, in_3[3], in_2[3]);
  nand nand_17 (nand_17_out, nand_5_out, nand_6_out);
  not nand_18 (nand_18_out, nand_7_out);  // NAND_Gate
  nand nand_19 (nand_19_out, nand_8_out, nand_9_out);
  not nand_20 (nand_20_out, nand_10_out);  // NAND_Gate
  nand nand_21 (nand_21_out, nand_11_out, nand_12_out);
  not nand_22 (nand_22_out, nand_13_out);  // NAND_Gate
  nand nand_23 (nand_23_out, nand_14_out, nand_15_out);
  not nand_24 (nand_24_out, nand_16_out);  // NAND_Gate
  nand nand_25 (nand_25_out, nand_21_out, nand_58_out);
  nand nand_26 (nand_26_out, nand_23_out, nand_59_out);
  nand nand_27 (nand_27_out, nand_17_out, in_1);
  nand nand_28 (nand_28_out, nand_19_out, nand_57_out);
  nand nand_29 (nand_29_out, nand_21_out, nand_25_out);
  nand nand_30 (nand_30_out, nand_25_out, nand_58_out);
  nand nand_31 (nand_31_out, nand_21_out, nand_58_out);
  nand nand_32 (nand_32_out, nand_23_out, nand_26_out);
  nand nand_33 (nand_33_out, nand_26_out, nand_59_out);
  nand nand_34 (nand_34_out, nand_23_out, nand_59_out);
  nand nand_35 (nand_35_out, nand_17_out, nand_27_out);
  nand nand_36 (nand_36_out, nand_27_out, in_1);
  nand nand_37 (nand_37_out, nand_17_out, in_1);
  nand nand_38 (nand_38_out, nand_19_out, nand_28_out);
  nand nand_39 (nand_39_out, nand_28_out, nand_57_out);
  nand nand_40 (nand_40_out, nand_19_out, nand_57_out);
  nand nand_41 (out_5[2], nand_29_out, nand_30_out);
  not nand_42 (nand_42_out, nand_31_out);  // NAND_Gate
  nand nand_43 (out_5[3], nand_32_out, nand_33_out);
  not nand_44 (nand_44_out, nand_34_out);  // NAND_Gate
  nand nand_45 (out_5[0], nand_35_out, nand_36_out);
  not nand_46 (nand_46_out, nand_37_out);  // NAND_Gate
  nand nand_47 (out_5[1], nand_38_out, nand_39_out);
  not nand_48 (nand_48_out, nand_40_out);  // NAND_Gate
  nand nand_49 (nand_49_out, nand_42_out, nand_42_out);
  nand nand_50 (nand_50_out, nand_22_out, nand_22_out);
  nand nand_51 (nand_51_out, nand_44_out, nand_44_out);
  nand nand_52 (nand_52_out, nand_24_out, nand_24_out);
  nand nand_53 (nand_53_out, nand_46_out, nand_46_out);
  nand nand_54 (nand_54_out, nand_18_out, nand_18_out);
  nand nand_55 (nand_55_out, nand_48_out, nand_48_out);
  nand nand_56 (nand_56_out, nand_20_out, nand_20_out);
  nand nand_57 (nand_57_out, nand_53_out, nand_54_out);
  nand nand_58 (nand_58_out, nand_55_out, nand_56_out);
  nand nand_59 (nand_59_out, nand_49_out, nand_50_out);
  nand nand_60 (Acarreo_final, nand_51_out, nand_52_out);

  assign out_5[4] = Acarreo_final;

  // Notes on the sheet:
  //   Circuito para SUMADOR de 4 BITS Usando solo Compuertas NAND
  //   Resultado final
endmodule
